# Fritzing sketch codos_WeMos_D1_Mini_Pro_esquemático (saved by Fritzing 0.9.3b)

parts:
  WeMos_D1_Mini1 = WeMos D1 Mini
  WS2812B1 = WS2812B 12V Strip -- White (60/m)
  U1 = STM811 [package=sot143]  # not connected
  Mod1 = CJMCU-811

nets:
  3V3: WeMos_D1_Mini1.3V3, Mod1.VCC
  N1: WeMos_D1_Mini1.5V, WS2812B1.DI
  N2: WeMos_D1_Mini1.D1, Mod1.SCL
  N3: WeMos_D1_Mini1.D2, Mod1.SDA
  N4: WeMos_D1_Mini1.D3, WS2812B1.+12V
  GND: WeMos_D1_Mini1.G, WS2812B1.GND, Mod1.GND, Mod1.WAK

custom parts:
  WS2812B 12V Strip -- White (60/m): WS2812B LED Strip, White, 60 pixels per meter, 12V Power
  CJMCU-811: The CCS811 is an ultra-low power digital gas sensor solution which integrates a metal oxide (MOX) gas sensor to detect a wide range of Volatile Organic Compounds (VOCs) for indoor air quality monitoring with a microcontroller unit (MCU), which includes an Analog-to-Digital converter (ADC), and an I²C interface.
